// Logisim project CPU.circ as structural Verilog: 1 circuit, main circuit main
module main (
  input  in_1
);

  wire Branch, clock_1_out, comparator_1_eq, main_1_alusrc, main_1_boz, main_1_branch, main_1_memr,
       main_1_memtoreg, main_1_memw, main_1_regdes, main_1_regwrite, nand_1_out;
  wire [3:0] multiplexer_1_out, rom_1_data;
  wire [15:0] adder_1_out, bit_extender_1_out, bit_extender_2_out, bit_extender_3_out, main_2_rs_data,
       main_2_rt_data, main_3_alu_out, multiplexer_2_out, multiplexer_3_out, multiplexer_4_out,
       multiplexer_5_out, multiplier_1_out, Pc_q, ram_1_data;
  wire [15:4] rom_1_data_2;

  Clock clock_1 (.out(clock_1_out));
  Register #(.width(16)) Pc (.D(multiplexer_4_out), .Q(Pc_q), .clk(clock_1_out), .clr(in_1));  // open: en
  CtrlUnit_main main_1 (
    .OpCode(rom_1_data), .branch(main_1_branch), .regWrite(main_1_regwrite), .RegDes(main_1_regdes),
    .AluSrc(main_1_alusrc), .MemR(main_1_memr), .MemW(main_1_memw), .MemToReg(main_1_memtoreg),
    .boz(main_1_boz));
  Adder #(.width(16)) adder_1 (.a(16'h2), .b(Pc_q), .out(adder_1_out));  // open: cin, cout
  ROM #(.addrWidth(16), .dataWidth(16)) rom_1 (.addr(Pc_q), .data({rom_1_data_2, rom_1_data}));  // open: sel
  Comparator #(.width(16)) comparator_1 (.a({16{1'b0}}), .b(main_2_rs_data), .eq(comparator_1_eq));  // open: gt, lt
  Multiplexer #(.width(4), .disabled(0), .enable("false")) multiplexer_1 (
    .in0(rom_1_data_2[11:8]), .in1(rom_1_data_2[15:12]), .out(multiplexer_1_out), .sel(main_1_regdes));
  assign bit_extender_1_out = {{12{rom_1_data_2[15]}}, rom_1_data_2[15:12]};  // Bit_Extender bit_extender_1
  nand nand_1 (nand_1_out, comparator_1_eq, main_1_boz);
  assign bit_extender_2_out = {{8{1'b0}}, rom_1_data_2[15:8]};  // Bit_Extender bit_extender_2
  assign bit_extender_3_out = {{4{1'b0}}, rom_1_data_2};  // Bit_Extender bit_extender_3
  Register_File_2_0_main main_2 (
    .RegWrite(main_1_regwrite), .Rd(multiplexer_1_out), .WriteData(multiplexer_5_out),
    .Rs(rom_1_data_2[7:4]), .Rt(rom_1_data_2[11:8]), .Clock(clock_1_out), .Rs_Data(main_2_rs_data),
    .Rt_Data(main_2_rt_data));
  Multiplexer #(.width(16), .disabled(0), .enable("false")) multiplexer_2 (
    .in0(main_2_rt_data), .in1(bit_extender_1_out), .out(multiplexer_2_out), .sel(main_1_alusrc));
  Multiplexer #(.width(16), .enable("false")) multiplexer_3 (
    .in0(bit_extender_3_out), .in1(bit_extender_2_out), .out(multiplexer_3_out), .sel(nand_1_out));
  ALU_main main_3 (.In1(main_2_rs_data), .In2(multiplexer_2_out), .OpCode(rom_1_data), .ALU_out(main_3_alu_out));
  Multiplier #(.width(16)) multiplier_1 (.a(multiplexer_3_out), .b(16'h2), .out(multiplier_1_out));  // open: cin, cout
  Multiplexer #(.width(16), .disabled(0), .enable("false")) multiplexer_4 (
    .in0(adder_1_out), .in1(multiplier_1_out), .out(multiplexer_4_out), .sel(Branch));
  RAM #(.addrWidth(16), .dataWidth(16), .bus("separate")) ram_1 (
    .addr(main_3_alu_out), .din(main_2_rt_data), .data(ram_1_data), .str(main_1_memw), .clk(clock_1_out),
    .ld(main_1_memr));  // open: sel, clr
  Multiplexer #(.width(16), .disabled(0), .enable("false")) multiplexer_5 (
    .in0(main_3_alu_out), .in1(ram_1_data), .out(multiplexer_5_out), .sel(main_1_memtoreg));
endmodule
